// Logisim project FSM.circ as structural Verilog: 4 circuits, main circuit FSM
module FSM (
  input  FSM_Input,
  output out_2
);

  wire clock_1_out;
  wire [1:0] fsmlogic_1_next_state, register_1_q;

  Register #(.width(2)) register_1 (.D(fsmlogic_1_next_state), .clk(clock_1_out), .Q(register_1_q));  // open: en, clr
  Clock clock_1 (.out(clock_1_out));
  FSMLogic fsmlogic_1 (
    .Input_Bit(FSM_Input), .Current_State(register_1_q), .Output(out_2), .Next_State(fsmlogic_1_next_state));
endmodule

// FSM Logic
module FSMLogic (
  input  Input_Bit,
  input  [1:0] Current_State,
  output Output,
  output [1:0] Next_State
);

  wire and_1_out, and_2_out, not_1_out, not_2_out, not_3_out;

  not not_1 (not_1_out, Current_State[1]);
  not not_2 (not_2_out, Input_Bit);
  not not_3 (not_3_out, Current_State[0]);
  and and_1 (and_1_out, Input_Bit, not_1_out);
  or or_1 (Output, and_1_out, and_2_out);
  and and_2 (and_2_out, not_2_out, not_3_out);
  StateBitZero statebitzero_1 (
    .Next_State_Bit_0(Next_State[0]), .FSM_Input(Input_Bit), .State_Bit_0(Current_State[0]),
    .State_Bit_1(Current_State[1]));
  StateBitOne statebitone_1 (
    .Next_State_Bit_1(Next_State[1]), .FSM_Input(Input_Bit), .State_Bit_0(Current_State[0]),
    .State_Bit_1(Current_State[1]));

  // Other names for the same wires on the sheet: Currrent_State_0 = Current_State[0];
  //   Current_State_1 = Current_State[1]
endmodule

// State Bit 1
module StateBitOne (
  input  FSM_Input,
  input  State_Bit_0,
  input  State_Bit_1,
  output Next_State_Bit_1
);

  wire and_1_out, not_1_out;

  not not_1 (not_1_out, State_Bit_0);
  and and_1 (and_1_out, FSM_Input, not_1_out);
  or or_1 (Next_State_Bit_1, and_1_out, State_Bit_0);

  // Other names for the same wires on the sheet: FSM_In = FSM_Input; Next_St1 = Next_State_Bit_1; St0 = State_Bit_0;
  //   St1 = State_Bit_1

  // Notes on the sheet:
  //   ------------------------------------------ Put your circuit below this line ------------------
endmodule

// State Bit 0
module StateBitZero (
  input  FSM_Input,
  input  State_Bit_0,
  input  State_Bit_1,
  output Next_State_Bit_0
);

  wire not_1_out, or_1_out;

  or or_1 (or_1_out, FSM_Input, State_Bit_1);
  not not_1 (not_1_out, or_1_out);
  or or_2 (Next_State_Bit_0, not_1_out, State_Bit_1);

  // Other names for the same wires on the sheet: FSM_In = FSM_Input; Next_St0 = Next_State_Bit_0; St0 = State_Bit_0;
  //   St1 = State_Bit_1

  // Notes on the sheet:
  //   ------------------------------------------ Put your circuit below this line ------------------
endmodule
