// Logisim project shr.circ as structural Verilog
module shr (
  input  [7:0] In_A,
  input  [2:0] In_B,
  input  in_3,
  input  in_4,
  input  in_5,
  output [7:0] R
);

  wire [7:0] multiplexer_1_out, multiplexer_2_out;

  Multiplexer #(.width(8), .enable("false")) multiplexer_1 (
    .in0(In_A), .in1({in_3, In_A[7:1]}), .out(multiplexer_1_out), .sel(In_B[0]));
  Multiplexer #(.width(8), .enable("false")) multiplexer_2 (
    .in0(multiplexer_1_out), .in1({{2{in_4}}, multiplexer_1_out[7:2]}), .out(multiplexer_2_out), .sel(In_B[1]));
  Multiplexer #(.width(8), .enable("false")) multiplexer_3 (
    .in0(multiplexer_2_out), .in1({{4{in_5}}, multiplexer_2_out[7:4]}), .out(R), .sel(In_B[2]));

  // Other names for the same wires on the sheet: A[7:0] = In_A; B[2:0] = In_B; Result[7:0] = R

  // Notes on the sheet:
  //   ------------------------- Put your circuit below this line ------------------
endmodule
